// Logisim project projetoLogico.circ as structural Verilog: 1 circuit, main circuit main
module main (
);

  wire and_1_out, and_2_out, and_3_out, and_4_out, and_5_out, and_6_out, button_1_out, d_ff_1_q, d_ff_1_qn,
       d_ff_2_q, d_ff_2_qn, d_ff_3_q, d_ff_3_qn, or_1_out, or_2_out, or_3_out, xor_1_out;

  and and_1 (and_1_out, d_ff_2_q, d_ff_3_q);
  xor xor_1 (xor_1_out, d_ff_2_q, d_ff_3_q);
  and and_2 (and_2_out, d_ff_1_qn, d_ff_3_qn);
  Button button_1 (.out(button_1_out));
  D_Flip_Flop d_ff_1 (.D(and_1_out), .clk(button_1_out), .Q(d_ff_1_q), .Qn(d_ff_1_qn));  // open: preset, reset
  D_Flip_Flop d_ff_2 (.D(xor_1_out), .clk(button_1_out), .Q(d_ff_2_q), .Qn(d_ff_2_qn));  // open: preset, reset
  D_Flip_Flop d_ff_3 (.D(and_2_out), .clk(button_1_out), .Q(d_ff_3_q), .Qn(d_ff_3_qn));  // open: preset, reset
  and and_3 (and_3_out, d_ff_2_q, d_ff_3_q);
  and and_4 (and_4_out, d_ff_1_q, d_ff_2_qn);
  and and_5 (and_5_out, d_ff_2_q, d_ff_3_qn);
  and and_6 (and_6_out, d_ff_2_qn, d_ff_3_q);
  or or_1 (or_1_out, and_3_out, and_4_out);
  or or_2 (or_2_out, and_4_out, and_5_out);
  or or_3 (or_3_out, and_4_out, and_6_out);
  LED led_1 (.in(or_1_out));
  LED led_2 (.in(or_1_out));
  LED led_3 (.in(or_2_out));
  LED led_4 (.in(or_3_out));
endmodule
