// Logisim project Implementacao.circ as structural Verilog: 1 circuit, main circuit main
module main (
);

  wire n7408_1_pin1, n7408_1_pin2, n7408_1_pin4, n7408_1_pin5, n7408_1_pin10, n7432_1_pin1, n7432_1_pin2,
       n7432_1_pin3, n7432_1_pin8, n7432_1_pin10, n7432_1_pin11, n7432_1_pin13, n7474_1_pin11, n7474_1_pin12,
       n7474_2_pin2, n7474_2_pin8, n7474_2_pin12;

  LED led_1 (.in(n7432_1_pin8));
  LED led_2 (.in(n7432_1_pin8));
  LED led_3 (.in(n7432_1_pin11));
  LED led_4 (.in(n7432_1_pin3));
  _7432 u_7432_1 (
    .pin1(n7432_1_pin1), .pin2(n7432_1_pin2), .pin3(n7432_1_pin3), .pin13(n7432_1_pin13),
    .pin12(n7432_1_pin2), .pin11(n7432_1_pin11), .pin10(n7432_1_pin10), .pin9(n7432_1_pin2),
    .pin8(n7432_1_pin8));  // open: pin4, pin5, pin6
  _7408 u_7408_1 (
    .pin1(n7408_1_pin1), .pin2(n7408_1_pin2), .pin3(n7432_1_pin10), .pin4(n7408_1_pin4), .pin5(n7408_1_pin5),
    .pin6(n7432_1_pin2), .pin13(n7408_1_pin1), .pin12(n7408_1_pin4), .pin11(n7432_1_pin1),
    .pin10(n7408_1_pin10), .pin9(n7408_1_pin2), .pin8(n7432_1_pin13));
  _7474 u_7474_1 (
    .pin12(n7474_1_pin12), .pin11(n7474_1_pin11), .pin9(n7408_1_pin1), .pin8(n7408_1_pin10));  // open: pin1, pin2, pin3, pin4, pin5, pin6, pin13, pin10
  _7474 u_7474_2 (
    .pin2(n7474_2_pin2), .pin3(n7474_1_pin11), .pin5(n7408_1_pin2), .pin6(n7408_1_pin4),
    .pin12(n7474_2_pin12), .pin11(n7474_1_pin11), .pin9(n7408_1_pin5), .pin8(n7474_2_pin8));  // open: pin1, pin4, pin13, pin10
  Button button_1 (.out(n7474_1_pin11));
  _7486 u_7486_1 (
    .pin10(n7408_1_pin2), .pin9(n7408_1_pin1), .pin8(n7474_2_pin2));  // open: pin1, pin2, pin3, pin4, pin5, pin6, pin13, pin12, pin11
  _7408 u_7408_2 (
    .pin4(n7408_1_pin10), .pin5(n7474_2_pin8), .pin6(n7474_1_pin12), .pin10(n7408_1_pin2),
    .pin9(n7408_1_pin1), .pin8(n7474_2_pin12));  // open: pin1, pin2, pin3, pin13, pin12, pin11
endmodule
